# Fritzing sketch can_motor_controller (saved by Fritzing 0.9.6b)
circuit board: 6.34895cm x 4.51192cm
perfboards: 1

parts:
  J3 = female pin header, 6 pins [form="♀ (female)"]
  Part1 = Logic Level Converter
  J5 = male pin header, 5 pins [form="♂ (male)"]
  J1 = Generic female header - 20 pins [form="♀ (female)" package=THT]
  J2 = female pin header, 7 pins [form="♀ (female)"]
  J4 = male pin header, 5 pins [form="♂ (male)"]

nets:
  5V: J3.pin1, Part1.LV, J1.5V
  GND: J3.pin2, Part1.GND, J5.pin1, J5.pin2, J5.pin3, J5.pin4, J5.pin5, J1.GND, J2.pin2
  CAN_TX: J3.pin3, J1.A12
  CAN_RX: J3.pin4, J1.A11
  CAN_HIGH: J3.pin5
  CAN_LOW: J3.pin6
  MOTOR_BRK_HV: Part1.TX2_LV, J2.pin4
  MOTOR_SIGNAL_HV: Part1.RX2_LV, J2.pin1
  MOTOR_STOP_HV: Part1.RX_LV, J2.pin5
  MOTOR_DIR_HV: Part1.TX_LV, J2.pin3
  MOTOR_DIR_LV: Part1.TX_HV, J1.A8
  MOTOR_STOP_LV: Part1.RX_HV, J1.B14
  3.3V: Part1.HV, J1.3.3v
  MOTOR_SIGNAL_LV: Part1.RX2_HV, J1.A10
  MOTOR_BRK_LV: Part1.TX2_HV, J1.B15
  BACK_LEFT_WHEEL: J1.B9, J4.pin4
  BACK_RIGHT_WHEEL: J1.B8, J4.pin5
  FRONT_RIGHT_WHEEL: J1.B7, J4.pin3
  FRONT_LEFT_WHEEL: J1.B6, J4.pin2
  MOTOR_ENCODER: J1.B13, J2.pin7

custom parts:
  Generic female header - 20 pins: Generic female header
